// Logisim project CPU.circ as structural Verilog: 7 circuits, main circuit DE0-CV
module DE0_CV (
);

  wire K0, K1, K2, K3, L0, L1, L2, L3, L4, L5, L6, L7, L8, L9, S0, S1, S2, S3, S4, S5, S6, S7, S8, S9;
  wire [3:0] HEX0, HEX1, HEX2, HEX3, HEX4, HEX5;

  Hex_Digit_Display hex_digit_display_1 (.value(HEX5));  // open: dp
  LED u_L9 (.in(L9));
  // DipSwitch #(.NSwitches(1)) S8: pin names not known; wires that end beside it: S8
  // DipSwitch #(.NSwitches(1)) S9: pin names not known; wires that end beside it: S9
  Hex_Digit_Display hex_digit_display_2 (.value(HEX4));  // open: dp
  LED u_L7 (.in(L7));
  LED u_L8 (.in(L8));
  LED u_L6 (.in(L6));
  // DipSwitch #(.NSwitches(1)) S7: pin names not known; wires that end beside it: S7
  // DipSwitch #(.NSwitches(1)) S6: pin names not known; wires that end beside it: S6
  Hex_Digit_Display hex_digit_display_3 (.value(HEX3));  // open: dp
  Hex_Digit_Display hex_digit_display_4 (.value(HEX2));  // open: dp
  LED u_L3 (.in(L3));
  LED u_L4 (.in(L4));
  LED u_L5 (.in(L5));
  // DipSwitch #(.NSwitches(1)) S4: pin names not known; wires that end beside it: S4
  // DipSwitch #(.NSwitches(1)) S3: pin names not known; wires that end beside it: S3
  // DipSwitch #(.NSwitches(1)) S5: pin names not known; wires that end beside it: S5
  Hex_Digit_Display hex_digit_display_5 (.value(HEX0));  // open: dp
  Hex_Digit_Display hex_digit_display_6 (.value(HEX1));  // open: dp
  LED u_L2 (.in(L2));
  LED u_L1 (.in(L1));
  // DipSwitch #(.NSwitches(1)) S2: pin names not known; wires that end beside it: S2
  // DipSwitch #(.NSwitches(1)) S1: pin names not known; wires that end beside it: S1
  // DipSwitch #(.NSwitches(1)) S0: pin names not known; wires that end beside it: S0
  LED u_L0 (.in(L0));
  Button u_K3 (.out(K3));
  Button u_K2 (.out(K2));
  Button u_K0 (.out(K0));
  Button u_K1 (.out(K1));
endmodule

module CPU (
  output [7:0] Entrada_1,
  output [15:0] \Saída_1 
);

  wire and_1_out, K0, K1, K2, K3, L8, L9, S0, S1, S2, S3, S4, S5, S6, S7, S8, S9;
  wire [3:0] HEX0, HEX1;

  LED u_L9 (.in(L9));
  // DipSwitch #(.NSwitches(1)) S9: pin names not known; wires that end beside it: S9
  Hex_Digit_Display hex_digit_display_1 (.value(\Saída_1 [11:8]));  // open: dp
  Hex_Digit_Display hex_digit_display_2 (.value(\Saída_1 [15:12]));  // open: dp
  LED L7 (.in(Entrada_1[7]));
  LED u_L8 (.in(L8));
  // DipSwitch #(.NSwitches(1)) S7: pin names not known; wires that end beside it: S7
  // DipSwitch #(.NSwitches(1)) S8: pin names not known; wires that end beside it: S8
  // DipSwitch #(.NSwitches(1)) S6: pin names not known; wires that end beside it: S6
  Hex_Digit_Display hex_digit_display_3 (.value(\Saída_1 [3:0]));  // open: dp
  Hex_Digit_Display hex_digit_display_4 (.value(\Saída_1 [7:4]));  // open: dp
  LED L6 (.in(Entrada_1[6]));
  LED L5 (.in(Entrada_1[5]));
  LED L4 (.in(Entrada_1[4]));
  // DipSwitch #(.NSwitches(1)) S4: pin names not known; wires that end beside it: S4
  // DipSwitch #(.NSwitches(1)) S5: pin names not known; wires that end beside it: S5
  Hex_Digit_Display hex_digit_display_5 (.value(HEX1));  // open: dp
  LED L2 (.in(Entrada_1[2]));
  LED L3 (.in(Entrada_1[3]));
  LED L1 (.in(Entrada_1[1]));
  // DipSwitch #(.NSwitches(1)) S3: pin names not known; wires that end beside it: S3
  // DipSwitch #(.NSwitches(1)) S1: pin names not known; wires that end beside it: S1
  // DipSwitch #(.NSwitches(1)) S2: pin names not known; wires that end beside it: S2
  Hex_Digit_Display hex_digit_display_6 (.value(HEX0));  // open: dp
  LED L0 (.in(Entrada_1[0]));
  // DipSwitch #(.NSwitches(1)) S0: pin names not known; wires that end beside it: S0
  Button u_K3 (.out(K3));
  Button u_K1 (.out(K1));
  Button u_K2 (.out(K2));
  Button u_K0 (.out(K0));
  and and_1 (and_1_out, \Saída_1 [10], \Saída_1 [11]);
  Contador_Sincrono_8_Bits contador_sincrono_8_bits_1 (
    .Clear(S0), .Jump(and_1_out), .Clock(S9), .Addr(\Saída_1 [3:0]), .Cont(Entrada_1));
  ROM_1 rom_1_1 (.\Barramento_de_Endereços (Entrada_1), .Barramento_de_Dados(\Saída_1 ));

  // Other names for the same wires on the sheet: Disponivel[3:0] = \Saída_1 [7:4]; HEX3[3:0] = \Saída_1 [7:4];
  //   Saida1[15:0] = \Saída_1 ; E1[7:0] = Entrada_1; L0 = Entrada_1[0]; L1 = Entrada_1[1]; L2 = Entrada_1[2];
  //   L3 = Entrada_1[3]; L4 = Entrada_1[4]; L5 = Entrada_1[5]; L6 = Entrada_1[6]; L7 = Entrada_1[7];
  //   HEX4[3:0] = \Saída_1 [11:8]; JMP[1:0] = \Saída_1 [11:10]; HEX2[3:0] = \Saída_1 [3:0];
  //   Operando[3:0] = \Saída_1 [3:0]; HEX5[3:0] = \Saída_1 [15:12]; RgIN[1:0] = \Saída_1 [13:12];
  //   RgTO[1:0] = \Saída_1 [15:14]; ULA[1:0] = \Saída_1 [9:8]
endmodule

module Contador_Sincrono_8_Bits (
  input  [3:0] Addr,
  input  Jump,
  input  Clock,
  input  Clear,
  output [7:0] Cont
);

  wire and_1_out, and_2_out, and_3_out, and_4_out, and_5_out, and_6_out, not_1_out;

  Flip_Flop_T_com_Jump ff_t_com_jump_1 (
    .Addr(Addr[0]), .Jump(Jump), .Clock(Clock), .T(1'b1), .Clear(not_1_out), .Q(Cont[0]));
  not not_1 (not_1_out, Clear);
  Flip_Flop_T_com_Jump ff_t_com_jump_2 (
    .Addr(Addr[1]), .Jump(Jump), .Clock(Clock), .T(Cont[0]), .Clear(not_1_out), .Q(Cont[1]));
  and and_1 (and_1_out, Cont[1], Cont[0]);
  Flip_Flop_T_com_Jump ff_t_com_jump_3 (
    .Addr(Addr[2]), .Jump(Jump), .Clock(Clock), .T(and_1_out), .Clear(not_1_out), .Q(Cont[2]));
  and and_2 (and_2_out, Cont[2], and_1_out);
  Flip_Flop_T_com_Jump ff_t_com_jump_4 (
    .Addr(Addr[3]), .Jump(Jump), .Clock(Clock), .T(and_2_out), .Clear(not_1_out), .Q(Cont[3]));
  and and_3 (and_3_out, Cont[3], and_2_out);
  Flip_Flop_T_com_Jump ff_t_com_jump_5 (
    .Addr(1'b0), .Jump(Jump), .Clock(Clock), .T(and_3_out), .Clear(not_1_out), .Q(Cont[4]));
  and and_4 (and_4_out, Cont[4], and_3_out);
  Flip_Flop_T_com_Jump ff_t_com_jump_6 (
    .Addr(1'b0), .Jump(Jump), .Clock(Clock), .T(and_4_out), .Clear(not_1_out), .Q(Cont[5]));
  and and_5 (and_5_out, Cont[5], and_4_out);
  Flip_Flop_T_com_Jump ff_t_com_jump_7 (
    .Addr(1'b0), .Jump(Jump), .Clock(Clock), .Clear(not_1_out), .Q(Cont[6]));  // open: T
  and and_6 (and_6_out, Cont[6], and_5_out);
  Flip_Flop_T_com_Jump ff_t_com_jump_8 (
    .Addr(1'b0), .Jump(Jump), .Clock(Clock), .T(and_6_out), .Clear(not_1_out), .Q(Cont[7]));
endmodule

module Flip_Flop_T_com_Jump (
  input  Addr,
  input  Jump,
  input  Clock,
  input  T,
  input  Clear,
  output Q
);

  wire and_1_out, nand_1_out, not_1_out, or_1_out;

  not not_1 (not_1_out, Jump);
  nand nand_1 (nand_1_out, Addr, Jump);
  or or_1 (or_1_out, Addr, not_1_out);
  and and_1 (and_1_out, or_1_out, Clear);
  T_Flip_Flop #(.NegatePresetClear("true")) t_ff_1 (
    .clk(Clock), .T(T), .Q(Q), .preset(nand_1_out), .reset(and_1_out));  // open: Qn
endmodule

module Registrador_4_Bits (
  input  Clock,
  input  Load,
  input  D3,
  input  D2,
  input  D1,
  input  D0,
  output Q3,
  output Q2,
  output Q1,
  output Q0
);

  wire multiplexer_1_out, multiplexer_2_out;

  Multiplexer #(.enable("false")) multiplexer_1 (.in0(Q3), .in1(D3), .out(multiplexer_1_out), .sel(Load));
  D_Flip_Flop d_ff_1 (.clk(Clock), .D(multiplexer_1_out), .Q(Q3));  // open: Qn, preset, reset
  Multiplexer #(.enable("false")) multiplexer_2 (.in0(Q2), .in1(D2), .out(multiplexer_2_out), .sel(Load));
  D_Flip_Flop d_ff_2 (.clk(Clock), .D(multiplexer_2_out), .Q(Q2));  // open: Qn, preset, reset
  Multiplexer #(.enable("false")) multiplexer_3 (.in0(Q1), .in1(D1), .sel(Load));  // open: out
  D_Flip_Flop d_ff_3 (.clk(Clock), .Q(Q1));  // open: D, Qn, preset, reset
  Multiplexer #(.enable("false")) multiplexer_4 (.in0(Q0), .in1(D0), .sel(Load));  // open: out
  D_Flip_Flop d_ff_4 (.clk(Clock), .Q(Q0));  // open: D, Qn, preset, reset
endmodule

module ROM_1 (
  input  [7:0] \Barramento_de_Endereços ,
  output [15:0] Barramento_de_Dados
);

  ROM #(.dataWidth(16), .Select("low")) \Memória_1  (
    .addr(\Barramento_de_Endereços ), .data(Barramento_de_Dados), .sel(1'b0));

  // Notes on the sheet:
  //   contents of Memória_1 (hex, n*v repeats v):
  //   6005 9101 6202 6304 c08 0 0 0 400 6001 9001 9002 6302 6102 9302 6200 6001 800
endmodule

module ROM_2 (
  input  [7:0] \Barramento_de_Endereços ,
  output [15:0] Barramento_de_Dados
);

  ROM #(.dataWidth(16), .Select("low")) \Memória_2  (
    .addr(\Barramento_de_Endereços ), .data(Barramento_de_Dados), .sel(1'b0));

  // Notes on the sheet:
  //   contents of Memória_2 (hex, n*v repeats v):
  //   6004 9102 6201 6305 9002 6002 9003 400 c0d 4*0 9002 6302 6101 9302 6200 6003 800
endmodule
